// Logisim project 25csb1a45_palak_COA.circ as structural Verilog: 1 circuit, main circuit main
module main (
  input  [1:0] FABRIC,
  input  [1:0] LOAD,
  input  [1:0] WATER,
  input  SOIL,
  input  [1:0] TURB,
  input  [1:0] BAL,
  input  FIXED_CYCLE,
  input  ADAPT_EN,
  input  BAL_EN,
  input  START,
  input  RESET,
  output IDLE,
  output WASH,
  output RINSE,
  output SPIN,
  output REBAL,
  output END,
  output FAULT,
  output OVER_BASELINE,
  output [2:0] STATE,
  output [7:0] TIMER,
  output [1:0] EXT_COUNT,
  output [1:0] BAL_RETRY,
  output [7:0] WASH_TIME,
  output [7:0] RINSE_TIME,
  output [7:0] SPIN_TIME,
  output [7:0] TOTAL_TICKS,
  output [11:0] ENERGY_USED,
  output [7:0] WATER_USED,
  output [7:0] TICKS_SAVED,
  output [11:0] ENERGY_SAVED,
  output [7:0] WATER_SAVED
);

  wire abort_all, adapt_eff, adapt_lat, adapt_live, att_ge, att_lt, bad_abort, bad_retry, bal_bad, bal_eff,
       bal_hi, bal_lat, bal_live, bal_ok, busy, chg, clk, count_en, e_over, end_rel, ext_ev, ext_lt, ext_no,
       ext_ok, ext_r, ext_w, f1, fabric_is1, fabric_is2, fabric_is3, fault_next, fixed_n, go_wash, load_is1,
       load_is2, load_is3, n1, n2, n3, n4, n5, n6, pre_abort, pre_rebal, rebal_all, rebal_end, rinse_end,
       rinse_fill, s_inval, spin_abort, spin_rebal, start_n, t_over, tnz, to_end, to_rinse, to_spin,
       to_spin_any, to_spin_ok, turb_hi, tz, w_over, wash_end, water_is1, water_is2, water_is3;
  wire [1:0] a1, att_inc, att_next, e_inc, ext_next, x1;
  wire [2:0] ns1, ns2, ns3, ns4, ns5, ns6, ns7, state_next;
  wire [7:0] fill_lat, fill_live, k1, ld_v, ld_x2, lv_a, lv_b, rinse_calc, rinse_lat, rinse_live, sb_a, sb_b,
       soil_add, spin_base, spin_calc, spin_lat, spin_live, t1, t2, t3, t4, t5, t6, t_dec, t_sub, t_sv, tb,
       ticks_inc, ticks_next, timer_next, w1, w_add, w_sub, w_sum, w_sv, wash_base, wash_calc, wash_lat,
       wash_live, water_fill, water_next, wb_a, wb_b, wl_v, wl_x2, wv_a, wv_b;
  wire [11:0] e_add, e_sub, e_sv, ei1, ei2, ei3, einc, energy_next, m1;

  Clock u_CLK (.out(clk));
  Comparator #(.width(2), .mode("unsigned")) comparator_1 (.a(FABRIC), .b(2'b01), .eq(fabric_is1));  // open: gt, lt
  Comparator #(.width(2), .mode("unsigned")) comparator_2 (.a(FABRIC), .b(2'b10), .eq(fabric_is2));  // open: gt, lt
  Comparator #(.width(2), .mode("unsigned")) comparator_3 (.a(FABRIC), .b(2'b11), .eq(fabric_is3));  // open: gt, lt
  Comparator #(.width(2), .mode("unsigned")) comparator_4 (.a(LOAD), .b(2'b01), .eq(load_is1));  // open: gt, lt
  Comparator #(.width(2), .mode("unsigned")) comparator_5 (.a(LOAD), .b(2'b10), .eq(load_is2));  // open: gt, lt
  Comparator #(.width(2), .mode("unsigned")) comparator_6 (.a(LOAD), .b(2'b11), .eq(load_is3));  // open: gt, lt
  Comparator #(.width(2), .mode("unsigned")) comparator_7 (.a(WATER), .b(2'b01), .eq(water_is1));  // open: gt, lt
  Comparator #(.width(2), .mode("unsigned")) comparator_8 (.a(WATER), .b(2'b10), .eq(water_is2));  // open: gt, lt
  Comparator #(.width(2), .mode("unsigned")) comparator_9 (.a(WATER), .b(2'b11), .eq(water_is3));  // open: gt, lt
  Comparator #(.width(3), .mode("unsigned")) comparator_10 (.a(STATE), .b(3'b000), .eq(IDLE));  // open: gt, lt
  Comparator #(.width(3), .mode("unsigned")) comparator_11 (.a(STATE), .b(3'b001), .eq(WASH));  // open: gt, lt
  Comparator #(.width(3), .mode("unsigned")) comparator_12 (.a(STATE), .b(3'b010), .eq(RINSE));  // open: gt, lt
  Comparator #(.width(3), .mode("unsigned")) comparator_13 (.a(STATE), .b(3'b011), .eq(SPIN));  // open: gt, lt
  Comparator #(.width(3), .mode("unsigned")) comparator_14 (.a(STATE), .b(3'b100), .eq(END));  // open: gt, lt
  Comparator #(.width(3), .mode("unsigned")) comparator_15 (.a(STATE), .b(3'b101), .eq(REBAL));  // open: gt, lt
  Comparator #(.width(3), .mode("unsigned")) comparator_16 (.a(STATE), .b(3'b101), .gt(s_inval));  // open: eq, lt
  Comparator #(.width(8), .mode("unsigned")) comparator_17 (.a(TIMER), .b({8{1'b0}}), .gt(tnz), .eq(tz));  // open: lt
  Comparator #(.width(2), .mode("unsigned")) comparator_18 (.a(TURB), .b(2'b01), .gt(turb_hi));  // open: eq, lt
  Comparator #(.width(2), .mode("unsigned")) comparator_19 (.a(BAL), .b(2'b01), .gt(bal_hi));  // open: eq, lt
  Comparator #(.width(2), .mode("unsigned")) comparator_20 (.a(EXT_COUNT), .b(2'b11), .lt(ext_lt));  // open: gt, eq
  Comparator #(.width(2), .mode("unsigned")) comparator_21 (.a(BAL_RETRY), .b(2'b10), .lt(att_lt));  // open: gt, eq
  Comparator #(.width(8), .mode("unsigned")) comparator_22 (.a(TOTAL_TICKS), .b(8'h31), .gt(t_over));  // open: eq, lt
  Comparator #(.width(12), .mode("unsigned")) comparator_23 (.a(ENERGY_USED), .b(12'h70), .gt(e_over));  // open: eq, lt
  Comparator #(.width(8), .mode("unsigned")) comparator_24 (.a(WATER_USED), .b(8'h10), .gt(w_over));  // open: eq, lt
  // Multiplexer #(.width(8)) multiplexer_1: pin names not known; wires that end beside it: 8'h8, 8'h6, fabric_is1, wb_a
  // Multiplexer #(.width(8)) multiplexer_2: pin names not known; wires that end beside it: wb_a, 8'h4, fabric_is2, wb_b
  // Multiplexer #(.width(8)) multiplexer_3: pin names not known; wires that end beside it: wb_b, 8'hc, fabric_is3, wash_base
  // Multiplexer #(.width(8)) multiplexer_4: pin names not known; wires that end beside it: 8'h6, 8'h5, fabric_is1, sb_a
  // Multiplexer #(.width(8)) multiplexer_5: pin names not known; wires that end beside it: sb_a, 8'h2, fabric_is2, sb_b
  // Multiplexer #(.width(8)) multiplexer_6: pin names not known; wires that end beside it: sb_b, 8'h8, fabric_is3, spin_base
  // Multiplexer #(.width(8)) multiplexer_7: pin names not known; wires that end beside it: 8'h1, 8'h2, load_is1, lv_a
  // Multiplexer #(.width(8)) multiplexer_8: pin names not known; wires that end beside it: lv_a, 8'h3, load_is2, lv_b
  // Multiplexer #(.width(8)) multiplexer_9: pin names not known; wires that end beside it: lv_b, 8'h4, load_is3, ld_v
  // Multiplexer #(.width(8)) multiplexer_10: pin names not known; wires that end beside it: 8'h1, 8'h2, water_is1, wv_a
  // Multiplexer #(.width(8)) multiplexer_11: pin names not known; wires that end beside it: wv_a, 8'h3, water_is2, wv_b
  // Multiplexer #(.width(8)) multiplexer_12: pin names not known; wires that end beside it: wv_b, 8'h4, water_is3, wl_v
  // Multiplexer #(.width(8)) multiplexer_13: pin names not known; wires that end beside it: {8{1'b0}}, 8'h4, SOIL, soil_add
  Multiplier #(.width(8)) multiplier_1 (.a(ld_v), .b(8'h2), .out(ld_x2), .cin({8{1'b0}}));  // open: cout
  Adder #(.width(8)) adder_1 (.a(wash_base), .b(ld_x2), .out(w_sum), .cin(1'b0));  // open: cout
  Adder #(.width(8)) adder_2 (.a(w_sum), .b(soil_add), .out(wash_calc), .cin(1'b0));  // open: cout
  Multiplier #(.width(8)) multiplier_2 (.a(wl_v), .b(8'h2), .out(wl_x2), .cin({8{1'b0}}));  // open: cout
  Adder #(.width(8)) adder_3 (.a(wl_x2), .b(8'h2), .out(rinse_calc), .cin(1'b0));  // open: cout
  Adder #(.width(8)) adder_4 (.a(spin_base), .b(ld_v), .out(spin_calc), .cin(1'b0));  // open: cout
  // Multiplexer #(.width(8)) multiplexer_14: pin names not known; wires that end beside it: wash_calc, 8'h18, FIXED_CYCLE, wash_live
  // Multiplexer #(.width(8)) multiplexer_15: pin names not known; wires that end beside it: rinse_calc, 8'ha, FIXED_CYCLE, rinse_live
  // Multiplexer #(.width(8)) multiplexer_16: pin names not known; wires that end beside it: spin_calc, 8'hc, FIXED_CYCLE, spin_live
  // Multiplexer #(.width(8)) multiplexer_17: pin names not known; wires that end beside it: wl_x2, 8'h8, FIXED_CYCLE, fill_live
  Subtractor #(.width(8)) subtractor_1 (.a(TIMER), .b(8'h1), .out(t_dec), .bin(1'b0));  // open: bout
  Adder #(.width(2)) adder_5 (.a(EXT_COUNT), .b(2'b01), .out(e_inc), .cin(1'b0));  // open: cout
  Adder #(.width(2)) adder_6 (.a(BAL_RETRY), .b(2'b01), .out(att_inc), .cin(1'b0));  // open: cout
  // Multiplexer #(.width(1)) multiplexer_18: pin names not known; wires that end beside it: 1'b1, 1'b0, FIXED_CYCLE, fixed_n
  // Multiplexer #(.width(1)) multiplexer_19: pin names not known; wires that end beside it: 1'b0, fixed_n, ADAPT_EN, adapt_live
  // Multiplexer #(.width(1)) multiplexer_20: pin names not known; wires that end beside it: 1'b0, fixed_n, BAL_EN, bal_live
  // Multiplexer #(.width(1)) multiplexer_21: pin names not known; wires that end beside it: RINSE, 1'b1, WASH, n1
  // Multiplexer #(.width(1)) multiplexer_22: pin names not known; wires that end beside it: SPIN, 1'b1, n1, n2
  // Multiplexer #(.width(1)) multiplexer_23: pin names not known; wires that end beside it: REBAL, 1'b1, n2, busy
  // Multiplexer #(.width(1)) multiplexer_24: pin names not known; wires that end beside it: 1'b0, tnz, busy, count_en
  // Multiplexer #(.width(1)) multiplexer_25: pin names not known; wires that end beside it: 1'b0, START, IDLE, go_wash
  // Multiplexer #(.width(1)) multiplexer_26: pin names not known; wires that end beside it: 1'b1, 1'b0, START, start_n
  // Multiplexer #(.width(1)) multiplexer_27: pin names not known; wires that end beside it: 1'b0, start_n, END, end_rel
  // Multiplexer #(.width(1)) multiplexer_28: pin names not known; wires that end beside it: 1'b0, tz, WASH, wash_end
  // Multiplexer #(.width(1)) multiplexer_29: pin names not known; wires that end beside it: 1'b0, tz, RINSE, rinse_end
  // Multiplexer #(.width(1)) multiplexer_30: pin names not known; wires that end beside it: 1'b0, tz, SPIN, to_end
  // Multiplexer #(.width(1)) multiplexer_31: pin names not known; wires that end beside it: 1'b0, tz, REBAL, rebal_end
  // Multiplexer #(.width(1)) multiplexer_32: pin names not known; wires that end beside it: 1'b0, ext_lt, turb_hi, n3
  // Multiplexer #(.width(1)) multiplexer_33: pin names not known; wires that end beside it: 1'b0, n3, adapt_eff, ext_ok
  // Multiplexer #(.width(1)) multiplexer_34: pin names not known; wires that end beside it: 1'b1, 1'b0, ext_ok, ext_no
  // Multiplexer #(.width(1)) multiplexer_35: pin names not known; wires that end beside it: 1'b0, ext_ok, wash_end, ext_w
  // Multiplexer #(.width(1)) multiplexer_36: pin names not known; wires that end beside it: 1'b0, ext_ok, rinse_end, ext_r
  // Multiplexer #(.width(1)) multiplexer_37: pin names not known; wires that end beside it: ext_r, 1'b1, ext_w, ext_ev
  // Multiplexer #(.width(1)) multiplexer_38: pin names not known; wires that end beside it: 1'b0, ext_no, wash_end, to_rinse
  // Multiplexer #(.width(1)) multiplexer_39: pin names not known; wires that end beside it: 1'b0, ext_no, rinse_end, to_spin
  // Multiplexer #(.width(1)) multiplexer_40: pin names not known; wires that end beside it: rebal_end, 1'b1, to_spin, to_spin_any
  // Multiplexer #(.width(1)) multiplexer_41: pin names not known; wires that end beside it: to_spin, 1'b1, to_rinse, n4
  // Multiplexer #(.width(1)) multiplexer_42: pin names not known; wires that end beside it: n4, 1'b1, go_wash, chg
  Register #(.width(8)) WASH_LATCH (.D(wash_live), .en(IDLE), .clk(clk), .Q(wash_lat), .clr(RESET));
  // Multiplexer #(.width(8)) multiplexer_43: pin names not known; wires that end beside it: wash_lat, wash_live, IDLE, WASH_TIME
  Register #(.width(8)) RINSE_LATCH (.D(rinse_live), .en(IDLE), .clk(clk), .Q(rinse_lat), .clr(RESET));
  // Multiplexer #(.width(8)) multiplexer_44: pin names not known; wires that end beside it: rinse_lat, rinse_live, IDLE, RINSE_TIME
  Register #(.width(8)) SPIN_LATCH (.D(spin_live), .en(IDLE), .clk(clk), .Q(spin_lat), .clr(RESET));
  // Multiplexer #(.width(8)) multiplexer_45: pin names not known; wires that end beside it: spin_lat, spin_live, IDLE, SPIN_TIME
  Register #(.width(8)) FILL_LATCH (.D(fill_live), .en(IDLE), .clk(clk), .Q(fill_lat), .clr(RESET));
  // Multiplexer #(.width(8)) multiplexer_46: pin names not known; wires that end beside it: fill_lat, fill_live, IDLE, water_fill
  Register #(.width(1)) ADAPT_LATCH (.D(adapt_live), .en(IDLE), .clk(clk), .Q(adapt_lat), .clr(RESET));
  // Multiplexer #(.width(1)) multiplexer_47: pin names not known; wires that end beside it: adapt_lat, adapt_live, IDLE, adapt_eff
  Register #(.width(1)) BAL_LATCH (.D(bal_live), .en(IDLE), .clk(clk), .Q(bal_lat), .clr(RESET));
  // Multiplexer #(.width(1)) multiplexer_48: pin names not known; wires that end beside it: bal_lat, bal_live, IDLE, bal_eff
  // Multiplexer #(.width(1)) multiplexer_49: pin names not known; wires that end beside it: 1'b0, bal_hi, bal_eff, bal_bad
  // Multiplexer #(.width(1)) multiplexer_50: pin names not known; wires that end beside it: 1'b1, 1'b0, bal_bad, bal_ok
  // Multiplexer #(.width(1)) multiplexer_51: pin names not known; wires that end beside it: 1'b1, 1'b0, att_lt, att_ge
  // Multiplexer #(.width(1)) multiplexer_52: pin names not known; wires that end beside it: 1'b0, att_lt, bal_bad, bad_retry
  // Multiplexer #(.width(1)) multiplexer_53: pin names not known; wires that end beside it: 1'b0, att_ge, bal_bad, bad_abort
  // Multiplexer #(.width(1)) multiplexer_54: pin names not known; wires that end beside it: 1'b0, bad_retry, SPIN, spin_rebal
  // Multiplexer #(.width(1)) multiplexer_55: pin names not known; wires that end beside it: 1'b0, bad_abort, SPIN, spin_abort
  // Multiplexer #(.width(1)) multiplexer_56: pin names not known; wires that end beside it: 1'b0, bal_ok, to_spin_any, to_spin_ok
  // Multiplexer #(.width(1)) multiplexer_57: pin names not known; wires that end beside it: 1'b0, bad_retry, to_spin_any, pre_rebal
  // Multiplexer #(.width(1)) multiplexer_58: pin names not known; wires that end beside it: 1'b0, bad_abort, to_spin_any, pre_abort
  // Multiplexer #(.width(1)) multiplexer_59: pin names not known; wires that end beside it: pre_rebal, 1'b1, spin_rebal, rebal_all
  // Multiplexer #(.width(1)) multiplexer_60: pin names not known; wires that end beside it: pre_abort, 1'b1, spin_abort, abort_all
  // Multiplexer #(.width(2)) multiplexer_61: pin names not known; wires that end beside it: BAL_RETRY, att_inc, rebal_all, a1
  // Multiplexer #(.width(2)) multiplexer_62: pin names not known; wires that end beside it: a1, 2'b00, go_wash, att_next
  // Multiplexer #(.width(1)) multiplexer_63: pin names not known; wires that end beside it: abort_all, 1'b1, FAULT, f1
  // Multiplexer #(.width(1)) multiplexer_64: pin names not known; wires that end beside it: f1, 1'b0, go_wash, fault_next
  // Multiplexer #(.width(3)) multiplexer_65: pin names not known; wires that end beside it: STATE, 3'b001, go_wash, ns1
  // Multiplexer #(.width(3)) multiplexer_66: pin names not known; wires that end beside it: ns1, 3'b010, to_rinse, ns2
  // Multiplexer #(.width(3)) multiplexer_67: pin names not known; wires that end beside it: ns2, 3'b011, to_spin_ok, ns3
  // Multiplexer #(.width(3)) multiplexer_68: pin names not known; wires that end beside it: ns3, 3'b100, to_end, ns4
  // Multiplexer #(.width(3)) multiplexer_69: pin names not known; wires that end beside it: ns4, 3'b101, rebal_all, ns5
  // Multiplexer #(.width(3)) multiplexer_70: pin names not known; wires that end beside it: ns5, 3'b100, abort_all, ns6
  // Multiplexer #(.width(3)) multiplexer_71: pin names not known; wires that end beside it: ns6, 3'b000, end_rel, ns7
  // Multiplexer #(.width(3)) multiplexer_72: pin names not known; wires that end beside it: ns7, 3'b000, s_inval, state_next
  // Multiplexer #(.width(8)) multiplexer_73: pin names not known; wires that end beside it: TIMER, t_dec, count_en, tb
  // Multiplexer #(.width(8)) multiplexer_74: pin names not known; wires that end beside it: tb, WASH_TIME, go_wash, t1
  // Multiplexer #(.width(8)) multiplexer_75: pin names not known; wires that end beside it: t1, 8'h3, ext_ev, t2
  // Multiplexer #(.width(8)) multiplexer_76: pin names not known; wires that end beside it: t2, RINSE_TIME, to_rinse, t3
  // Multiplexer #(.width(8)) multiplexer_77: pin names not known; wires that end beside it: t3, SPIN_TIME, to_spin_ok, t4
  // Multiplexer #(.width(8)) multiplexer_78: pin names not known; wires that end beside it: t4, 8'h4, rebal_all, t5
  // Multiplexer #(.width(8)) multiplexer_79: pin names not known; wires that end beside it: t5, {8{1'b0}}, abort_all, t6
  // Multiplexer #(.width(8)) multiplexer_80: pin names not known; wires that end beside it: t6, {8{1'b0}}, s_inval, timer_next
  // Multiplexer #(.width(2)) multiplexer_81: pin names not known; wires that end beside it: EXT_COUNT, e_inc, ext_ev, x1
  // Multiplexer #(.width(2)) multiplexer_82: pin names not known; wires that end beside it: x1, 2'b00, chg, ext_next
  Adder #(.width(8)) adder_7 (.a(TOTAL_TICKS), .b(8'h1), .out(ticks_inc), .cin(1'b0));  // open: cout
  // Multiplexer #(.width(8)) multiplexer_83: pin names not known; wires that end beside it: TOTAL_TICKS, ticks_inc, busy, k1
  // Multiplexer #(.width(8)) multiplexer_84: pin names not known; wires that end beside it: k1, {8{1'b0}}, go_wash, ticks_next
  // Multiplexer #(.width(12)) multiplexer_85: pin names not known; wires that end beside it: {12{1'b0}}, 12'h1, RINSE, ei1
  // Multiplexer #(.width(12)) multiplexer_86: pin names not known; wires that end beside it: ei1, 12'h3, WASH, ei2
  // Multiplexer #(.width(12)) multiplexer_87: pin names not known; wires that end beside it: ei2, 12'h2, SPIN, ei3
  // Multiplexer #(.width(12)) multiplexer_88: pin names not known; wires that end beside it: ei3, 12'h1, REBAL, einc
  Adder #(.width(12)) adder_8 (.a(ENERGY_USED), .b(einc), .out(e_add), .cin(1'b0));  // open: cout
  // Multiplexer #(.width(12)) multiplexer_89: pin names not known; wires that end beside it: ENERGY_USED, e_add, busy, m1
  // Multiplexer #(.width(12)) multiplexer_90: pin names not known; wires that end beside it: m1, {12{1'b0}}, go_wash, energy_next
  // Multiplexer #(.width(1)) multiplexer_91: pin names not known; wires that end beside it: ext_r, 1'b1, to_rinse, rinse_fill
  Adder #(.width(8)) adder_9 (.a(WATER_USED), .b(water_fill), .out(w_add), .cin(1'b0));  // open: cout
  // Multiplexer #(.width(8)) multiplexer_92: pin names not known; wires that end beside it: WATER_USED, w_add, rinse_fill, w1
  // Multiplexer #(.width(8)) multiplexer_93: pin names not known; wires that end beside it: w1, water_fill, go_wash, water_next
  Subtractor #(.width(8)) subtractor_2 (.a(8'h31), .b(TOTAL_TICKS), .out(t_sub), .bin(1'b0));  // open: bout
  // Multiplexer #(.width(8)) multiplexer_94: pin names not known; wires that end beside it: t_sub, {8{1'b0}}, t_over, t_sv
  // Multiplexer #(.width(8)) multiplexer_95: pin names not known; wires that end beside it: {8{1'b0}}, t_sv, END, TICKS_SAVED
  Subtractor #(.width(12)) subtractor_3 (.a(12'h70), .b(ENERGY_USED), .out(e_sub), .bin(1'b0));  // open: bout
  // Multiplexer #(.width(12)) multiplexer_96: pin names not known; wires that end beside it: e_sub, {12{1'b0}}, e_over, e_sv
  // Multiplexer #(.width(12)) multiplexer_97: pin names not known; wires that end beside it: {12{1'b0}}, e_sv, END, ENERGY_SAVED
  Subtractor #(.width(8)) subtractor_4 (.a(8'h10), .b(WATER_USED), .out(w_sub), .bin(1'b0));  // open: bout
  // Multiplexer #(.width(8)) multiplexer_98: pin names not known; wires that end beside it: w_sub, {8{1'b0}}, w_over, w_sv
  // Multiplexer #(.width(8)) multiplexer_99: pin names not known; wires that end beside it: {8{1'b0}}, w_sv, END, WATER_SAVED
  // Multiplexer #(.width(1)) multiplexer_100: pin names not known; wires that end beside it: e_over, 1'b1, t_over, n5
  // Multiplexer #(.width(1)) multiplexer_101: pin names not known; wires that end beside it: w_over, 1'b1, n5, n6
  // Multiplexer #(.width(1)) multiplexer_102: pin names not known; wires that end beside it: 1'b0, n6, END, OVER_BASELINE
  Register #(.width(3)) STATE_REG (.D(state_next), .en(1'b1), .clk(clk), .Q(STATE), .clr(RESET));
  Register #(.width(8)) TIMER_REG (.D(timer_next), .en(1'b1), .clk(clk), .Q(TIMER), .clr(RESET));
  Register #(.width(2)) EXT_REG (.D(ext_next), .en(1'b1), .clk(clk), .Q(EXT_COUNT), .clr(RESET));
  Register #(.width(2)) BAL_RETRY_REG (.D(att_next), .en(1'b1), .clk(clk), .Q(BAL_RETRY), .clr(RESET));
  Register #(.width(1)) FAULT_REG (.D(fault_next), .en(1'b1), .clk(clk), .Q(FAULT), .clr(RESET));
  Register #(.width(8)) TICKS_REG (.D(ticks_next), .en(1'b1), .clk(clk), .Q(TOTAL_TICKS), .clr(RESET));
  Register #(.width(12)) ENERGY_REG (.D(energy_next), .en(1'b1), .clk(clk), .Q(ENERGY_USED), .clr(RESET));
  Register #(.width(8)) WATER_REG (.D(water_next), .en(1'b1), .clk(clk), .Q(WATER_USED), .clr(RESET));

  // Other names for the same wires on the sheet: att[1:0] = BAL_RETRY; energy[11:0] = ENERGY_USED;
  //   ext[1:0] = EXT_COUNT; fixed = FIXED_CYCLE; over_base = OVER_BASELINE; s_end = END; s_idle = IDLE;
  //   s_rebal = REBAL; s_rinse = RINSE; s_spin = SPIN; s_wash = WASH; ticks[7:0] = TOTAL_TICKS

  // Notes on the sheet:
  //   Smart Washing Machine Control and Cycle Management System  |  Palak (25CSB1A45)  |  COA EC1263  |  Logisim Evolution 4.1.0  |  FIXED/audited build
  //   Features: closed-loop turbidity feedback (ADAPT_EN) + unbalance guard with bounded REBAL retries and FAULT (BAL_EN) + resource meter vs fixed-cycle baseline.  Enable ticks: Ctrl+K.
  //   Ablation: FIXED_CYCLE=1 -> B0 baseline | FIXED=0,ADAPT=0,BAL=0 -> B1 | +ADAPT_EN/+BAL_EN -> B2.  Fabric 0=cotton 1=synthetic 2=delicate 3=heavy.  States: 0 IDLE 1 WASH 2 RINSE 3 SPIN 4 END 5 REBAL (6,7 recover to IDLE).
  //   INPUTS
  //   Set switches, pulse START. RESET = async clear.
  //   DECODERS / COMPARATORS
  //   EQ against constants decodes STATE; GT/LT test thresholds.
  //   PARAMETER LOOK-UP (MUX)
  //   fabric/load/water -> constants via 2:1 mux chains.
  //   CYCLE-TIME ARITHMETIC
  //   wash = base + 2*load + 4*soil; rinse = 2*water+2; spin = base+load.
  //   CONTROL EVENTS (MUX LOGIC)
  //   go_wash = IDLE&START; stage ends = state&timer==0.
  //   CONFIG LATCH (frozen at START)
  //   Registers load every tick in IDLE, hold while running (WE=IDLE).
  //   UNBALANCE GUARD + FAULT
  //   Pre-spin + in-spin check; max 2 REBAL then FAULT.
  //   NEXT-STATE / NEXT-TIMER
  //   Priority chain: later mux wins (abort > rebal > end ...).
  //   RESOURCE METER + BASELINE
  //   ticks, energy (3/1/2/1 per tick), water; compare to 49/112/16.
  //   STATE REGISTERS
  //   Async RESET clears all. WE tied 1 (latch regs use WE=IDLE).
  //   OUTPUTS
  //   SAVED outputs valid at END only.
  //   Energy units/tick: WASH 3, RINSE 1, SPIN 2, REBAL 1. Baseline fixed program = 49 ticks, 112 energy, 16 water. SAVED outputs are valid at END (clamped at 0; OVER_BASELINE flags a run costing more).
endmodule
